# Fritzing sketch 3led_pwm (saved by Fritzing 0.9.3b)
breadboards: 1

parts:
  부품1 = Arduino Uno (Rev3)
  LED1 = LED - 5mm [color="Red (633nm)" package="5 mm [THT]"]
  LED4 = LED - 5mm [color="Green (560nm)" package="5 mm [THT]"]
  LED5 = LED - 5mm [color="Blue (470nm)" package="5 mm [THT]"]
  R2 = Resistor [tolerance=±5% resistance=330 package=THT]
  R3 = Resistor [tolerance=±5% resistance=330 package=THT]
  R4 = Resistor [tolerance=±5% resistance=330 package=THT]

nets:
  N1: 부품1.D3_PWM, LED1.anode
  N2: 부품1.D5_PWM, LED4.anode
  N3: 부품1.D6_PWM, LED5.anode
  N4: 부품1.GND, R2.Pin_0, R3.Pin_1, R4.Pin_1
  N5: LED1.cathode, R2.Pin_1
  N6: LED4.cathode, R3.Pin_0
  N7: LED5.cathode, R4.Pin_0
