# Fritzing sketch TMP36_CdS_LCD_circuit (saved by Fritzing 0.9.3b)
breadboards: 1

parts:
  부품1 = Arduino Uno (Rev3)
  LCD1 = LCD screen
  R1 = Rotary Potentiometer (Small) [maximum_resistance=100kΩ package=THT]
  R2 = Photocell (LDR) [package=THT]
  R3 = Resistor [tolerance=±5% resistance=10k package=THT]
  U1 = TMP36 [package=to-92-kit]

nets:
  N1: 부품1.A0, U1.VOUT
  N2: 부품1.A1, R2.pin_1, R3.Pin_0
  N3: 부품1.D11_PWM/MOSI, LCD1.E
  N4: 부품1.D12/MISO, LCD1.RS
  N5: 부품1.D2, LCD1.DB7
  N6: 부품1.D3_PWM, LCD1.DB6
  N7: 부품1.D4, LCD1.DB5
  N8: 부품1.D5_PWM, LCD1.DB4
  5V: 부품1.5V, LCD1.VDD, LCD1.LED+, R1.leg1, R3.Pin_1, U1.VCC
  GND: 부품1.GND, LCD1.VSS, LCD1.R/W, LCD1.LED-, R1.leg2, R2.pin_0, U1.GND
  N9: LCD1.V0, R1.wiper
