# Fritzing sketch TMP36_LDR_circuit (saved by Fritzing 0.9.3b)
breadboards: 1

parts:
  R1 = Resistor [tolerance=±5% resistance=10k package=THT]
  R2 = Photocell (LDR) [package=THT]
  부품1 = Arduino Uno (Rev3)
  T2 = TMP36 Temperature Sensor [package="TO92 [THT]"]

nets:
  N1: R1.Pin_0, R2.pin_1, 부품1.A1
  N2: R1.Pin_1, 부품1.5V, T2.+Vs
  GND: R2.pin_0, 부품1.GND, T2.GND
  N3: 부품1.A0, T2.Vout
