# Fritzing sketch DHT22_LDR_circuit (saved by Fritzing 0.9.3b)
breadboards: 1

parts:
  R1 = Resistor [tolerance=±5% resistance=10k package=THT]
  R2 = Photocell (LDR) [package=THT]
  부품1 = Arduino Uno (Rev3)
  RHT1 = Humidity and Temperature Sensor RHT03
  R3 = Resistor [tolerance=±5% resistance=1k package=THT]

nets:
  N1: R1.Pin_0, R2.pin_1, 부품1.A0
  5V: R1.Pin_1, 부품1.5V, RHT1.Vcc, R3.Pin_0
  N2: R2.pin_0, 부품1.GND, RHT1.GND_2
  N3: 부품1.D4, RHT1.Data-signal, R3.Pin_1
